# Fritzing sketch Versão(0.4) (saved by Fritzing 0.9.3b)
breadboards: 1

parts:
  Componente1 = Arduino Uno (Rev3)
  R1 = Resistor [tolerance=±5% resistance=220 package=THT]
  LED1 = LED - 5mm [color="Red (633nm)" package="5 mm [THT]"]
  HC-SR04_Sensor_1 = HC-SR04 Ultrasonic Distance Sensor
  U1 = LCD-16X2 [package=lcd-16x2_noholes]
  LCM1602_IIC1 = LCM1602 IIC [part_number="LCM1602 IIC" chip_label="LCM1602 IIC" package="DIP (Dual Inline) [THT]"]

nets:
  N1: Componente1.A4/SDA, LCM1602_IIC1.SDA
  N2: Componente1.A5/SCL, LCM1602_IIC1.SCL
  N3: Componente1.D4, HC-SR04_Sensor_1.TRIG
  N4: Componente1.D5_PWM, HC-SR04_Sensor_1.ECHO
  N5: Componente1.D7, LED1.anode
  VCC: Componente1.5V, HC-SR04_Sensor_1.VCC, LCM1602_IIC1.VCC
  GND: Componente1.GND, R1.Pin_1, HC-SR04_Sensor_1.GND, LCM1602_IIC1.GND
  N6: R1.Pin_0, LED1.cathode
  VSS: U1.VSS, LCM1602_IIC1.VSS
  VDD: U1.VDD, LCM1602_IIC1.VDD
  N7: U1.VO, LCM1602_IIC1.V0
  N8: U1.RS, LCM1602_IIC1.RS
  N9: U1.R_W, LCM1602_IIC1.RW
  N10: U1.E, LCM1602_IIC1.E
  N11: U1.DB0, LCM1602_IIC1.D0
  N12: U1.DB1, LCM1602_IIC1.D1
  N13: U1.DB2, LCM1602_IIC1.D2
  N14: U1.DB3, LCM1602_IIC1.D3
  N15: U1.DB4, LCM1602_IIC1.D4
  N16: U1.DB5, LCM1602_IIC1.D5
  N17: U1.DB6, LCM1602_IIC1.D6
  N18: U1.DB7, LCM1602_IIC1.D7
  N19: U1.A, LCM1602_IIC1.A
  N20: U1.K, LCM1602_IIC1.K
  N21: LCM1602_IIC1.LED_A, LCM1602_IIC1.LED_B

custom parts:
  LCM1602 IIC: I2C-Module to use a 1602 or 2004 LCD on with the wire.h libory Serial LCD Modul
